# Fritzing sketch NS1patch4adsr-vca-vcf (saved by Fritzing 0.9.2b)

parts:
  Componente1 = Ns1 Nanosynth by SoundMachines

nets:
  N1: Componente1.SQU, Componente1.GATE
  N2: Componente1.SAW, Componente1.→#145
  N3: Componente1.→#119, Componente1.OUT#132
  N4: Componente1.←#121, Componente1.CV#142
  N5: Componente1.→#126, Componente1.OUT#133
  N6: Componente1.←#127, Componente1.CV#150
  N7: Componente1.←LP, Componente1.→#149
  N8: Componente1.←#152, Componente1.AMP

notes:
  VCA INITIAL: 0
  The envelope generator (ADSR) is a very important module. Here you will learn how to use it against the VCA and VCF !
  VCF FREQ: 5 to 0
  VCF RESO: 7
  VCO FREQ: 2
  ADSR: start with all the params at zero except the sustain, then play with them to understand the effect!
  ATTEN1 regulates the amount of ADSR to the VCA. Start at 0 and slowly rise the amount. ATTEN2 regulates the amount to the FREQ of the filter. This

custom parts:
  Ns1 Nanosynth by SoundMachines: The NS1nanosynth synthesizer is tiny 220x85mm analog modular synthesizer coupled with an Arduino Micro platform. NS1nanosynth is a good compromise between complexity and usability. It's a Maker synth, totally hackable and customazable yet a good entry level device, and on a budget.
