# Fritzing sketch NS1patch7logic_clkburst (saved by Fritzing 0.9.2b)

parts:
  Componente1 = Ns1 Nanosynth by SoundMachines

nets:
  N1: Componente1.SQU, Componente1.N#74
  N2: Componente1.N#76, Componente1.CKDIV_←
  N3: Componente1.N#77, Componente1.AND_←#171
  N4: Componente1.SAW, Componente1.→#145
  N5: Componente1.→#119, Componente1.→#125
  N6: Componente1.→#120, Componente1.OUT
  N7: Componente1.←#121, Componente1.CV#150
  N8: Componente1.←#127, Componente1.CV#143
  N9: Componente1.GATE, Componente1.AND_→
  N10: Componente1.←LP, Componente1.→#149
  N11: Componente1.←#152, Componente1.AMP
  N12: Componente1.CKDIV_/4, Componente1.AND_←#170

notes:
  ADSR:
  attack:0, decay:10, sustain:0,release5)
  LFO1 freq: 7
  ATTEN1:5
  ATTEN2:5
  bursts of four notes will be played followed by a four notes pause
  VCA INITIAL: 3

custom parts:
  Ns1 Nanosynth by SoundMachines: The NS1nanosynth synthesizer is tiny 220x85mm analog modular synthesizer coupled with an Arduino Micro platform. NS1nanosynth is a good compromise between complexity and usability. It's a Maker synth, totally hackable and customazable yet a good entry level device, and on a budget.
